# Fritzing sketch pcb001 (saved by Fritzing 1.0.1rc)
circuit board: 8.00001cm x 8.00001cm
breadboards: 1

parts:
  U1 = Molex Picoblade Series Header [part_number=0532610219 package=Picoblade-53261-0219]
  U2 = Molex Picoblade Series Header [part_number=0532610219 package=Picoblade-53261-0219]
  U3 = Molex Picoblade Series Header [part_number=0532610219 package=Picoblade-53261-0219]
  J1 = Camdenboss CTB0158-2 [part_number=CTB0158-2 package=THT]
  J2 = Camdenboss CTB0158-2 [part_number=CTB0158-2 package=THT]
  J3 = Camdenboss CTB0158-2 [part_number=CTB0158-2 package=THT]

nets:
  N1: U1.1, U2.1, U3.1
  N2: U1.2, U2.2, U3.2
  N3: J1.pin1, J2.pin1, J3.pin1
  N4: J1.pin2, J2.pin2, J3.pin2

notes:
  info@n2048.com
